// Logisim project S2-T21.circ as structural Verilog: 5 circuits, main circuit main
module main (
  input  _0,
  input  _1,
  input  _2,
  input  _3,
  input  [3:0] in_5,
  input  _4,
  input  _5,
  input  _6,
  input  _7,
  input  _8,
  input  clk,
  input  reset,
  input  [3:0] source,
  input  [3:0] Destination,
  output _0_2,
  output _1_2,
  output _2_2,
  output _3_2,
  output _4_2,
  output _5_2,
  output _6_2,
  output _7_2,
  output _8_2,
  output out_24
);

  wire adder_1_cout, adj_matrix_1_output, comparator_1_lt, or_1_out;
  wire [3:0] adder_1_out, adj_matrix_1_node, distances_value1, distances_value2, multiplexer_1_out,
       multiplexer_2_out, multiplexer_3_out, multiplexer_4_out, multiplexer_5_out, parent_value1,
       parent_value2, queue_1_queue_top;

  adj_matrix adj_matrix_1 (
    ._0(_0), ._1(_1), ._2(_2), ._3(_3), ._4(_4), ._5(_5), ._6(_6), ._7(_7), ._8(_8), .clk(clk),
    .input_node(queue_1_queue_top), .Node(adj_matrix_1_node), .\output (adj_matrix_1_output));
  Multiplexer #(.width(4)) multiplexer_1 (
    .in0(in_5), .in1(adj_matrix_1_node), .out(multiplexer_1_out), .sel(adj_matrix_1_output));  // open: en
  Multiplexer #(.width(4)) multiplexer_2 (
    .in0(source), .in1(multiplexer_1_out), .out(multiplexer_2_out));  // open: sel, en
  Queue queue_1 (
    .\input (multiplexer_2_out), .clk(clk), .clear(reset), .queue_top(queue_1_queue_top), .queue_end(out_24));  // open: queue_read, reg_write, shift
  distance parent (
    .Node(multiplexer_1_out), .Reg_Clear(reset), .Distance(queue_1_queue_top), .Clk(clk),
    .Value1(parent_value1), .Value2(parent_value2), .Readno2(Destination), .Readno1(parent_value2));
  distance distances (
    .Node(multiplexer_1_out), .Reg_Clear(reset), .Distance(multiplexer_4_out), .Clk(clk),
    .Value1(distances_value1), .Value2(distances_value2), .Readno2(queue_1_queue_top),
    .Readno1(multiplexer_1_out));
  visitednodes visitednodes_1 (
    .Node(queue_1_queue_top), .Clock(clk), .RegClear(reset), .Input(1'b1));  // open: Output, ReadNode
  Multiplexer #(.width(4)) multiplexer_3 (
    .in0(parent_value1), .in1(Destination), .out(multiplexer_3_out), .sel(out_24));  // open: en
  Adder #(.width(4)) adder_1 (.a(distances_value2), .b(4'b0001), .out(adder_1_out), .cout(adder_1_cout));  // open: cin
  Multiplexer #(.width(4)) multiplexer_4 (
    .in0(multiplexer_5_out), .in1(4'b0000), .out(multiplexer_4_out));  // open: sel, en
  Comparator #(.width(4), .mode("unsigned")) comparator_1 (
    .a(distances_value1), .b(adder_1_out), .lt(comparator_1_lt));  // open: gt, eq
  Multiplexer #(.width(4)) multiplexer_5 (
    .in0(adder_1_out), .in1(distances_value1), .out(multiplexer_5_out), .sel(or_1_out));  // open: en
  Decoder #(.select(4)) decoder_1 (
    .out0(_0_2), .out1(_1_2), .out2(_2_2), .out3(_3_2), .out4(_4_2), .out5(_5_2), .out6(_6_2), .out7(_7_2),
    .out8(_8_2), .sel(multiplexer_3_out));  // open: out9, out10, out11, out12, out13, out14, out15, en
  or or_1 (or_1_out, adder_1_cout, comparator_1_lt);

  // Notes on the sheet:
  //   Input Nodes
  //   S2-T21 
  //   Pal Patel -231CS240 
  //   Pragya Paromita barma - 231CS241
  //   Srishti Kumari - 231CS258
  //   4. Reset button is for restting the whole algorithm 
  //   5. Simulate the clock frequency as input
  //   Instructions
  //   1.Turn on the switches which you want to take in as input
  //   2. Input the node number of source in binary in source switch
  //   3. Input the node number of destination in binary in destination switch
  //   Path Out
endmodule

module adj_matrix (
  input  _0,
  input  _1,
  input  _2,
  input  _3,
  input  _4,
  input  _5,
  input  _6,
  input  _7,
  input  _8,
  input  clk,
  input  [3:0] input_node,
  output [3:0] Node,
  output \output 
);

  wire not_1_out, not_2_out, not_3_out, not_4_out, not_5_out, not_6_out, not_7_out, not_8_out, not_9_out,
       ram_1_data, ram_2_data, ram_3_data, ram_4_data, ram_5_data, ram_6_data, ram_7_data, ram_8_data,
       ram_9_data, rom_1_data, rom_2_data, rom_3_data, rom_4_data, rom_5_data, rom_6_data, rom_7_data,
       rom_8_data, rom_9_data;

  Counter #(.width(4), .max('h8)) counter_1 (.Q(Node), .clk(clk));  // open: load, D, count, carry, clr
  ROM #(.addrWidth(4), .dataWidth(1)) rom_1 (.addr(Node), .data(rom_1_data));  // open: sel
  ROM #(.addrWidth(4), .dataWidth(1)) rom_2 (.addr(Node), .data(rom_2_data));  // open: sel
  ROM #(.addrWidth(4), .dataWidth(1)) rom_3 (.addr(Node), .data(rom_3_data));  // open: sel
  ROM #(.addrWidth(4), .dataWidth(1)) rom_4 (.addr(Node), .data(rom_4_data));  // open: sel
  ROM #(.addrWidth(4), .dataWidth(1)) rom_5 (.addr(Node), .data(rom_5_data));  // open: sel
  ROM #(.addrWidth(4), .dataWidth(1)) rom_6 (.addr(Node), .data(rom_6_data));  // open: sel
  ROM #(.addrWidth(4), .dataWidth(1)) rom_7 (.addr(Node), .data(rom_7_data));  // open: sel
  ROM #(.addrWidth(4), .dataWidth(1)) rom_8 (.addr(Node), .data(rom_8_data));  // open: sel
  ROM #(.addrWidth(4), .dataWidth(1)) rom_9 (.addr(Node), .data(rom_9_data));  // open: sel
  not not_1 (not_1_out, _0);
  not not_2 (not_2_out, _1);
  not not_3 (not_3_out, _2);
  not not_4 (not_4_out, _3);
  not not_5 (not_5_out, _4);
  not not_6 (not_6_out, _5);
  not not_7 (not_7_out, _6);
  not not_8 (not_8_out, _7);
  not not_9 (not_9_out, _8);
  RAM #(.addrWidth(4), .dataWidth(1), .bus("separate")) ram_1 (
    .addr(Node), .data(ram_1_data), .str(rom_1_data), .clk(clk), .clr(not_1_out));  // open: din, sel, ld
  RAM #(.addrWidth(4), .dataWidth(1), .bus("separate")) ram_2 (
    .addr(Node), .data(ram_2_data), .str(rom_2_data), .clk(clk), .clr(not_2_out));  // open: din, sel, ld
  RAM #(.addrWidth(4), .dataWidth(1), .bus("separate")) ram_3 (
    .addr(Node), .data(ram_3_data), .str(rom_3_data), .clk(clk), .clr(not_3_out));  // open: din, sel, ld
  RAM #(.addrWidth(4), .dataWidth(1), .bus("separate")) ram_4 (
    .addr(Node), .data(ram_4_data), .str(rom_4_data), .clk(clk), .clr(not_4_out));  // open: din, sel, ld
  RAM #(.addrWidth(4), .dataWidth(1), .bus("separate")) ram_5 (
    .addr(Node), .data(ram_5_data), .str(rom_5_data), .clk(clk), .clr(not_5_out));  // open: din, sel, ld
  RAM #(.addrWidth(4), .dataWidth(1), .bus("separate")) ram_6 (
    .addr(Node), .data(ram_6_data), .str(rom_6_data), .clk(clk), .clr(not_6_out));  // open: din, sel, ld
  RAM #(.addrWidth(4), .dataWidth(1), .bus("separate")) ram_7 (
    .addr(Node), .data(ram_7_data), .str(rom_7_data), .clk(clk), .clr(not_7_out));  // open: din, sel, ld
  RAM #(.addrWidth(4), .dataWidth(1), .bus("separate")) ram_8 (
    .addr(Node), .data(ram_8_data), .str(rom_8_data), .clk(clk), .clr(not_8_out));  // open: din, sel, ld
  RAM #(.addrWidth(4), .dataWidth(1), .bus("separate")) ram_9 (
    .addr(Node), .data(ram_9_data), .str(rom_9_data), .clk(clk), .clr(not_9_out));  // open: din, sel, ld
  Multiplexer #(.select(4)) multiplexer_1 (
    .in0(ram_1_data), .in1(ram_2_data), .in2(ram_3_data), .in3(ram_4_data), .in4(ram_5_data),
    .in5(ram_6_data), .in6(ram_7_data), .in7(ram_8_data), .in8(ram_9_data), .out(\output ), .sel(input_node));  // open: in9, in10, in11, in12, in13, in14, in15, en

  // Notes on the sheet:
  //   contents of rom_1 (hex, n*v repeats v):
  //   0 1 0 1
  //   contents of rom_2 (hex, n*v repeats v):
  //   1 0 1 0 1
  //   contents of rom_3 (hex, n*v repeats v):
  //   0 1 0 0 0 1
  //   contents of rom_4 (hex, n*v repeats v):
  //   1 0 0 0 1 0 1
  //   contents of rom_5 (hex, n*v repeats v):
  //   0 1 0 1 0 1 0 1
  //   contents of rom_6 (hex, n*v repeats v):
  //   0 0 1 0 1 0 0 0 1
  //   contents of rom_7 (hex, n*v repeats v):
  //   0 0 0 1 0 0 0 1
  //   contents of rom_8 (hex, n*v repeats v):
  //   4*0 1 0 1 0 1
  //   contents of rom_9 (hex, n*v repeats v):
  //   5*0 1 0 1
endmodule

// queue
module Queue (
  input  queue_read,
  input  [3:0] \input ,
  input  reg_write,
  input  clk,
  input  clear,
  input  shift,
  output [3:0] queue_top,
  output queue_end
);

  wire decoder_1_out0, decoder_1_out1, decoder_1_out2, decoder_1_out3, decoder_1_out4, decoder_1_out5,
       decoder_1_out6, decoder_1_out7, decoder_1_out8, or_1_out, or_2_out, or_3_out, or_4_out, or_5_out,
       or_6_out, or_7_out, or_8_out, or_9_out, or_10_out;
  wire [3:0] adder_1_out, multiplexer_1_out, multiplexer_2_out, multiplexer_3_out, multiplexer_4_out,
       multiplexer_5_out, multiplexer_6_out, multiplexer_7_out, multiplexer_8_out, multiplexer_9_out,
       multiplexer_10_out, register_1_q, register_2_q, register_3_q, register_4_q, register_5_q,
       register_6_q, register_7_q, register_8_q, register_9_q, subtractor_1_out, write_adr_q;

  Register #(.width(4)) write_adr (.D(multiplexer_1_out), .en(or_1_out), .Q(write_adr_q), .clk(clk), .clr(clear));
  or or_1 (or_1_out, reg_write, shift);
  Decoder #(.select(4), .disabled(0)) decoder_1 (
    .out0(decoder_1_out0), .out1(decoder_1_out1), .out2(decoder_1_out2), .out3(decoder_1_out3),
    .out4(decoder_1_out4), .out5(decoder_1_out5), .out6(decoder_1_out6), .out7(decoder_1_out7),
    .out8(decoder_1_out8), .sel(write_adr_q), .en(reg_write));  // open: out9, out10, out11, out12, out13, out14, out15
  Multiplexer #(.width(4), .enable("false")) multiplexer_1 (
    .in0(adder_1_out), .in1(subtractor_1_out), .out(multiplexer_1_out), .sel(shift));
  Adder #(.width(4)) adder_1 (.a(write_adr_q), .b(4'b0001), .out(adder_1_out));  // open: cin, cout
  Subtractor #(.width(4)) subtractor_1 (.a(write_adr_q), .b(4'b0001), .out(subtractor_1_out));  // open: bin, bout
  or or_2 (or_2_out, decoder_1_out0, shift);
  or or_3 (or_3_out, decoder_1_out1, shift);
  or or_4 (or_4_out, decoder_1_out2, shift);
  or or_5 (or_5_out, decoder_1_out3, shift);
  or or_6 (or_6_out, decoder_1_out4, shift);
  or or_7 (or_7_out, decoder_1_out5, shift);
  or or_8 (or_8_out, shift, decoder_1_out6);
  or or_9 (or_9_out, shift, decoder_1_out7);
  or or_10 (or_10_out, shift, decoder_1_out8);
  Multiplexer #(.width(4)) multiplexer_2 (
    .in0(\input ), .in1(register_2_q), .out(multiplexer_2_out), .sel(shift));  // open: en
  Multiplexer #(.width(4)) multiplexer_3 (
    .in0(\input ), .in1(register_3_q), .out(multiplexer_3_out), .sel(shift));  // open: en
  Multiplexer #(.width(4)) multiplexer_4 (
    .in0(\input ), .in1(register_4_q), .out(multiplexer_4_out), .sel(shift));  // open: en
  Multiplexer #(.width(4)) multiplexer_5 (
    .in0(\input ), .in1(register_5_q), .out(multiplexer_5_out), .sel(shift));  // open: en
  Multiplexer #(.width(4)) multiplexer_6 (
    .in0(\input ), .in1(register_6_q), .out(multiplexer_6_out), .sel(shift));  // open: en
  Multiplexer #(.width(4)) multiplexer_7 (
    .in0(\input ), .in1(register_7_q), .out(multiplexer_7_out), .sel(shift));  // open: en
  Multiplexer #(.width(4)) multiplexer_8 (
    .in0(\input ), .in1(register_8_q), .out(multiplexer_8_out), .sel(shift));  // open: en
  Multiplexer #(.width(4)) multiplexer_9 (
    .in0(\input ), .in1(register_9_q), .out(multiplexer_9_out), .sel(shift));  // open: en
  Multiplexer #(.width(4)) multiplexer_10 (
    .in0(\input ), .in1(4'b0000), .out(multiplexer_10_out), .sel(shift));  // open: en
  Register #(.width(4)) register_1 (.D(multiplexer_2_out), .en(or_2_out), .Q(register_1_q), .clk(clk), .clr(clear));
  Register #(.width(4)) register_2 (.D(multiplexer_3_out), .en(or_3_out), .Q(register_2_q), .clk(clk), .clr(clear));
  Register #(.width(4)) register_3 (.D(multiplexer_4_out), .en(or_4_out), .Q(register_3_q), .clk(clk), .clr(clear));
  Register #(.width(4)) register_4 (.D(multiplexer_5_out), .en(or_5_out), .Q(register_4_q), .clk(clk), .clr(clear));
  Register #(.width(4)) register_5 (.D(multiplexer_6_out), .en(or_6_out), .Q(register_5_q), .clk(clk), .clr(clear));
  Register #(.width(4)) register_6 (.D(multiplexer_7_out), .en(or_7_out), .Q(register_6_q), .clk(clk), .clr(clear));
  Register #(.width(4)) register_7 (.D(multiplexer_8_out), .en(or_8_out), .Q(register_7_q), .clk(clk), .clr(clear));
  Register #(.width(4)) register_8 (.D(multiplexer_9_out), .en(or_9_out), .Q(register_8_q), .clk(clk), .clr(clear));
  Register #(.width(4)) register_9 (.D(multiplexer_10_out), .en(or_10_out), .Q(register_9_q), .clk(clk), .clr(clear));
  Multiplexer #(.width(4)) multiplexer_11 (
    .in0(4'b0000), .in1(register_1_q), .out(queue_top), .sel(queue_read));  // open: en
  Comparator #(.width(4)) comparator_1 (.a(4'b0000), .b(write_adr_q), .eq(queue_end));  // open: gt, lt
endmodule

module distance (
  input  [3:0] Node,
  input  Reg_Clear,
  input  [3:0] Distance,
  input  [3:0] Readno2,
  input  Clk,
  input  [3:0] Readno1,
  output [3:0] Value1,
  output [3:0] Value2
);

  wire decoder_1_out0, decoder_1_out1, decoder_1_out2, decoder_1_out3, decoder_1_out4, decoder_1_out5,
       decoder_1_out6, decoder_1_out7, decoder_1_out8, or_1_out, or_2_out, or_3_out, or_4_out, or_5_out,
       or_6_out, or_7_out, or_8_out, or_9_out;
  wire [3:0] multiplexer_1_out, register_1_q, register_2_q, register_3_q, register_4_q, register_5_q,
       register_6_q, register_7_q, register_8_q, register_9_q;

  Decoder #(.select(4), .disabled(0)) decoder_1 (
    .out0(decoder_1_out0), .out1(decoder_1_out1), .out2(decoder_1_out2), .out3(decoder_1_out3),
    .out4(decoder_1_out4), .out5(decoder_1_out5), .out6(decoder_1_out6), .out7(decoder_1_out7),
    .out8(decoder_1_out8), .sel(Node));  // open: out9, out10, out11, out12, out13, out14, out15, en
  Multiplexer #(.width(4)) multiplexer_1 (
    .in0(Distance), .in1(4'b1111), .out(multiplexer_1_out), .sel(Reg_Clear));  // open: en
  or or_1 (or_1_out, decoder_1_out0, Reg_Clear);
  or or_2 (or_2_out, decoder_1_out1, Reg_Clear);
  or or_3 (or_3_out, decoder_1_out2, Reg_Clear);
  or or_4 (or_4_out, decoder_1_out3, Reg_Clear);
  or or_5 (or_5_out, Reg_Clear, decoder_1_out4);
  or or_6 (or_6_out, Reg_Clear, decoder_1_out5);
  or or_7 (or_7_out, Reg_Clear, decoder_1_out6);
  or or_8 (or_8_out, Reg_Clear, decoder_1_out7);
  or or_9 (or_9_out, Reg_Clear, decoder_1_out8);
  Register #(.width(4)) register_1 (.D(multiplexer_1_out), .en(or_1_out), .Q(register_1_q), .clk(Clk), .clr(1'b0));
  Register #(.width(4)) register_2 (.D(multiplexer_1_out), .en(or_2_out), .Q(register_2_q), .clk(Clk), .clr(1'b0));
  Register #(.width(4)) register_3 (.D(multiplexer_1_out), .en(or_3_out), .Q(register_3_q), .clk(Clk), .clr(1'b0));
  Register #(.width(4)) register_4 (.D(multiplexer_1_out), .en(or_4_out), .Q(register_4_q), .clk(Clk), .clr(1'b0));
  Register #(.width(4)) register_5 (.D(multiplexer_1_out), .en(or_5_out), .Q(register_5_q), .clk(Clk), .clr(1'b0));
  Register #(.width(4)) register_6 (.D(multiplexer_1_out), .en(or_6_out), .Q(register_6_q), .clk(Clk), .clr(1'b0));
  Register #(.width(4)) register_7 (.D(multiplexer_1_out), .en(or_7_out), .Q(register_7_q), .clk(Clk), .clr(1'b0));
  Register #(.width(4)) register_8 (.D(multiplexer_1_out), .en(or_8_out), .Q(register_8_q), .clk(Clk), .clr(1'b0));
  Register #(.width(4)) register_9 (.D(multiplexer_1_out), .en(or_9_out), .Q(register_9_q), .clk(Clk), .clr(1'b0));
  Multiplexer #(.select(4), .width(4)) multiplexer_2 (
    .in0(register_1_q), .in1(register_2_q), .in2(register_3_q), .in3(register_4_q), .in4(register_5_q),
    .in5(register_6_q), .in6(register_7_q), .in7(register_8_q), .in8(register_9_q), .out(Value1),
    .sel(Readno2));  // open: in9, in10, in11, in12, in13, in14, in15, en
  Multiplexer #(.select(4), .width(4)) multiplexer_3 (
    .in0(register_1_q), .in1(register_2_q), .in2(register_3_q), .in3(register_4_q), .in4(register_5_q),
    .in5(register_6_q), .in6(register_7_q), .in7(register_8_q), .in8(register_9_q), .out(Value2),
    .sel(Readno1));  // open: in9, in10, in11, in12, in13, in14, in15, en
endmodule

// visited
module visitednodes (
  input  [3:0] ReadNode,
  input  [3:0] Node,
  input  Clock,
  input  RegClear,
  input  Input,
  output Output
);

  wire decoder_1_out0, decoder_1_out1, decoder_1_out2, decoder_1_out3, decoder_1_out4, decoder_1_out5,
       decoder_1_out6, decoder_1_out7, decoder_1_out8, register_1_q, register_2_q, register_3_q,
       register_4_q, register_5_q, register_6_q, register_7_q, register_8_q, register_9_q;

  Decoder #(.select(4)) decoder_1 (
    .out0(decoder_1_out0), .out1(decoder_1_out1), .out2(decoder_1_out2), .out3(decoder_1_out3),
    .out4(decoder_1_out4), .out5(decoder_1_out5), .out6(decoder_1_out6), .out7(decoder_1_out7),
    .out8(decoder_1_out8), .sel(Node));  // open: out9, out10, out11, out12, out13, out14, out15, en
  Register #(.width(1)) register_1 (.D(Input), .en(decoder_1_out0), .Q(register_1_q), .clk(Clock), .clr(RegClear));
  Register #(.width(1)) register_2 (.D(Input), .en(decoder_1_out1), .Q(register_2_q), .clk(Clock), .clr(RegClear));
  Register #(.width(1)) register_3 (.D(Input), .en(decoder_1_out2), .Q(register_3_q), .clk(Clock), .clr(RegClear));
  Register #(.width(1)) register_4 (.D(Input), .en(decoder_1_out3), .Q(register_4_q), .clk(Clock), .clr(RegClear));
  Register #(.width(1)) register_5 (.D(Input), .en(decoder_1_out4), .Q(register_5_q), .clk(Clock), .clr(RegClear));
  Register #(.width(1)) register_6 (.D(Input), .en(decoder_1_out5), .Q(register_6_q), .clk(Clock), .clr(RegClear));
  Register #(.width(1)) register_7 (.D(Input), .en(decoder_1_out6), .Q(register_7_q), .clk(Clock), .clr(RegClear));
  Register #(.width(1)) register_8 (.D(Input), .en(decoder_1_out7), .Q(register_8_q), .clk(Clock), .clr(RegClear));
  Register #(.width(1)) register_9 (.D(Input), .en(decoder_1_out8), .Q(register_9_q), .clk(Clock), .clr(RegClear));
  Multiplexer #(.select(4)) multiplexer_1 (
    .in0(register_1_q), .in1(register_2_q), .in2(register_3_q), .in3(register_4_q), .in4(register_5_q),
    .in5(register_6_q), .in6(register_7_q), .in7(register_8_q), .in8(register_9_q), .out(Output),
    .sel(ReadNode));  // open: in9, in10, in11, in12, in13, in14, in15, en
endmodule
